# Fritzing sketch diagrama_THIS (saved by Fritzing 0.9.3b)
breadboards: 1

parts:
  J1 = Generic female header - 2 pins [form="♀ (female)" package=THT]
  J3 = Generic female header - 2 pins [form="♀ (female)" package=THT]
  J5 = Generic female header - 2 pins [form="♀ (female)" package=THT]
  Raspberry_Pi_1 = Raspberry Pi 3 [part_number=RPI-3-V1.2]
  J2 = Generic female header - 2 pins [form="♀ (female)" package=THT]
  J4 = Generic female header - 2 pins [form="♀ (female)" package=THT]

nets:
  GND: J1.GND, J3.GND, J5.GND, Raspberry_Pi_1.GND, J2.GND, J4.GND
  N1: J1.SCL, J3.SCL, Raspberry_Pi_1.GPIO3, J2.SCL
  N2: J1.SDA, J3.SDA, Raspberry_Pi_1.GPIO2, J2.SDA
  VCC: J3.VCC, J5.VCC, Raspberry_Pi_1.5V, J2.VCC
  N3: J3.A0, J4.SPL
  3V3: Raspberry_Pi_1.3V3, J4.VCC

custom parts:
  Generic female header - 2 pins: Generic female header
  Generic female header - 2 pins: Generic female header
  Generic female header - 2 pins: Generic female header
  Generic female header - 2 pins: Generic female header
  Generic female header - 2 pins: Generic female header
