# Fritzing sketch SensorH2O (saved by Fritzing 0.9.3b)
circuit board: 8.49064cm x 6.73172cm
breadboards: 1

parts:
  R1 = Resistor [tolerance=±5% resistance=1k package=THT]
  R2 = Resistor [tolerance=±5% resistance=1k package=THT]
  R3 = Resistor [tolerance=±5% resistance=1k package=THT]
  R4 = Resistor [tolerance=±5% resistance=1k package=THT]
  R5 = Resistor [tolerance=±5% resistance=1k package=THT]
  R6 = Resistor [tolerance=±5% resistance=1k package=THT]
  R7 = Resistor [tolerance=±5% resistance=1k package=THT]
  R8 = Resistor [tolerance=±5% resistance=1k package=THT]
  U2 = mystery part, 14 pins [chip_label=?]
  Componente1 = Adafruit Micro USB Breakout [part_number="Adafruit #1833"]
  M1 = DOIT Esp32 DevKit v1 (30 pins long, 11 pins width) [part_number=ESP32S-PIN30]
  J1 = female pin header, 8 pins [form="♀ (female)"]
  J2 = female pin header, 8 pins [form="♀ (female)"]
  S5 = female pin header, 1 pin [form="♀ (female)"]
  J3 = female pin header, 1 pin [form="♀ (female)"]
  J4 = female pin header, 1 pin [form="♀ (female)"]
  J5 = female pin header, 4 pins [form="♀ (female)"]
  S1 = female pin header, 1 pin [form="♀ (female)"]
  S2 = female pin header, 1 pin [form="♀ (female)"]
  J7 = female pin header, 1 pin [form="♀ (female)"]
  J8 = female pin header, 1 pin [form="♀ (female)"]
  J9 = female pin header, 1 pin [form="♀ (female)"]
  J6 = female pin header, 5 pins [form="♀ (female)"]
  J10 = female pin header, 1 pin [form="♀ (female)"]
  J11 = female pin header, 1 pin [form="♀ (female)"]
  J12 = female pin header, 1 pin [form="♀ (female)"]
  U1 = mystery part, 14 pins [chip_label=?]

nets:
  N1: R1.Pin_0, U2.pin7, M1.D15
  GND: R1.Pin_1, R2.Pin_1, R3.Pin_1, R4.Pin_1, R5.Pin_0, R6.Pin_0, R7.Pin_0, R8.Pin_0, U2.pin11, Componente1.GND, M1.GND, J2.pin1, J2.pin2, J2.pin3, J2.pin4, J2.pin5, J2.pin6, J2.pin7, J2.pin8, J4.pin1, U1.pin11
  N2: R2.Pin_0, U2.pin1, M1.D2
  N3: R3.Pin_0, M1.D4, U1.pin7
  N4: R4.Pin_0, M1.D5, J6.pin5
  N5: R5.Pin_1, M1.D18, J6.pin4
  N6: R6.Pin_1, M1.D21, J6.pin3
  N7: R7.Pin_1, M1.D23, J6.pin1
  N8: R8.Pin_1, M1.D22, J6.pin2
  N9: U2.pin2, S2.pin1
  N10: U2.pin3, U2.pin5, U2.pin10, U2.pin12, M1.3V3, U1.pin3, U1.pin5, U1.pin10, U1.pin12
  N11: U2.pin4, Componente1.VBUS, M1.VIN, J1.pin1, J1.pin2, J1.pin3, J1.pin4, J1.pin5, J1.pin6, J1.pin7, J1.pin8, J3.pin1, U1.pin4
  N12: U2.pin6, S1.pin1
  N13: U2.pin8, J5.pin1
  N14: U2.pin9, J12.pin1
  N15: U2.pin13, J11.pin1
  N16: U2.pin14, J5.pin2
  N17: S5.pin1, U1.pin13
  N18: J5.pin3, U1.pin8
  N19: J5.pin4, U1.pin14
  N20: J7.pin1, U1.pin6
  N21: J8.pin1, U1.pin2
  N22: J9.pin1, U1.pin1
  N23: J10.pin1, U1.pin9

custom parts:
  Adafruit Micro USB Breakout: Simple but effective - this breakout board has a USB Micro-B connector, with all 5 pins broken out. Great for pairing with a microcontroller with USB support, or adding USB 5V power to a project. We use a micro-AB connector with through-hole shielding pads for an excellent strong connection - it won't rip off by accident! Comes with one fully assembled and tested micro B breakout PCB and a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
  DOIT Esp32 DevKit v1 (30 pins long, 11 pins width): The DOIT Esp32 DevKit v1 is one of the development board created by DOIT to evaluate the ESP-WROOM-32 module. It is based on the ESP32 microcontroller that boasts Wifi, Bluetooth, Ethernet and Low Power support all in a single chip. (vanepp) made breadboard work, adjusted pin numbering and labels and reduced size of schematic and cleaned up pcb. This chip is 30pins long (2 x15) and 11 pins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
