# Fritzing sketch YF-S201 (saved by Fritzing 0.9.3b)
breadboards: 1

parts:
  YF-S201_Flow_Meter2 = YF-S201 Water Flow Meter
  X1 = USB Connectors [package=usb-minib-nostop]
  U1 = LM124-324 Quad Opamp [package="DIP (Dual Inline)"]
  U2 = NodeMCU V1.0
  R4 = Resistor [tolerance=±5% resistance=1k package="2512 [SMD]"]

nets:
  N1: YF-S201_Flow_Meter2.SIG, U1.3IN-
  N2: YF-S201_Flow_Meter2.GND, X1.D-, U1.VCC-, R4.Pin_0
  N3: YF-S201_Flow_Meter2.VCC, U1.VCC+
  N4: U1.1IN+, U1.4IN+, U2.3V3
  N5: U1.3OUT, U2.D4, R4.Pin_1

custom parts:
  YF-S201 Water Flow Meter: The YF-S201 Flow Meter. The input voltage is 5V to 24V (DC).
  NodeMCU V1.0: ESP8266 based NodeMCU
